// Logisim project cpu.circ as structural Verilog: 1 circuit, main circuit main
module main (
  input  [31:0] INSTRUCTION,
  input  CLOCK,
  output [31:0] PROGRAM_COUNTER,
  output [31:0] ra,
  output [31:0] sp,
  output [31:0] t0,
  output [31:0] t1,
  output [31:0] t2,
  output [31:0] s0,
  output [31:0] s1,
  output [31:0] a0
);

  wire branch_comp_1_breq, branch_comp_1_brlt, control_logic_1_asel, control_logic_1_brun,
       control_logic_1_bsel, control_logic_1_memrw, control_logic_1_pcsel, control_logic_1_regwen;
  wire [1:0] control_logic_1_wbsel;
  wire [2:0] control_logic_1_immsel;
  wire [3:0] control_logic_1_alusel;
  wire [4:0] rd, rs1, rs2;
  wire [31:0] adder_1_out, Arithmetic_Logic_Unit_result, DMEM_p5, imm_gen_1_imm, multiplexer_1_out,
       multiplexer_2_out, multiplexer_3_out, multiplexer_4_out, RegFile_read_data_1, RegFile_read_data_2,
       register_1_q;

  Register #(.width(32)) register_1 (
    .D(INSTRUCTION), .clk(CLOCK),
    .Q({register_1_q[31:25], rs2, rs1, register_1_q[14:12], rd, register_1_q[6:0]}));  // open: en, clr
  control_logic control_logic_1 (
    .BSel(control_logic_1_bsel), .RegWEn(control_logic_1_regwen), .ASel(control_logic_1_asel),
    .ImmSel(control_logic_1_immsel), .BrUn(control_logic_1_brun), .PCSel(control_logic_1_pcsel),
    .BrLt(branch_comp_1_brlt), .BrEq(branch_comp_1_breq),
    .inst({register_1_q[31:25], rs2, rs1, register_1_q[14:12], rd, register_1_q[6:0]}),
    .ALUSel(control_logic_1_alusel), .MemRW(control_logic_1_memrw), .WBSel(control_logic_1_wbsel));
  Multiplexer #(.width(32), .enable("false")) multiplexer_1 (
    .in0(adder_1_out), .in1(Arithmetic_Logic_Unit_result), .out(multiplexer_1_out),
    .sel(control_logic_1_pcsel));
  Adder #(.width(32)) adder_1 (.a(PROGRAM_COUNTER), .b(32'h4), .out(adder_1_out));  // open: cin, cout
  imm_gen imm_gen_1 (
    .ImmSel(control_logic_1_immsel), .imm(imm_gen_1_imm),
    .inst({register_1_q[31:25], rs2, rs1, register_1_q[14:12], rd, register_1_q[6:0]}));
  Register #(.width(32)) PC (.D(multiplexer_1_out), .clk(CLOCK), .Q(PROGRAM_COUNTER));  // open: en, clr
  regfile_main RegFile (
    .rs2(rs2), .rd(rd), .Read_Data_1(RegFile_read_data_1), .Read_Data_2(RegFile_read_data_2), .ra(ra),
    .sp(sp), .t0(t0), .t1(t1), .t2(t2), .s0(s0), .s1(s1), .a0(a0), .rs1(rs1), .Write_Data(multiplexer_4_out),
    .RegWEn(control_logic_1_regwen), .clk(CLOCK));
  branch_comp branch_comp_1 (
    .BrEq(branch_comp_1_breq), .BrUn(control_logic_1_brun), .rs1(RegFile_read_data_1),
    .BrLt(branch_comp_1_brlt), .rs2(RegFile_read_data_2));
  Multiplexer #(.width(32), .enable("false")) multiplexer_2 (
    .in0(RegFile_read_data_1), .in1(PROGRAM_COUNTER), .out(multiplexer_2_out), .sel(control_logic_1_asel));
  Multiplexer #(.width(32), .enable("false")) multiplexer_3 (
    .in0(RegFile_read_data_2), .in1(imm_gen_1_imm), .out(multiplexer_3_out), .sel(control_logic_1_bsel));
  alu Arithmetic_Logic_Unit (
    .ALUSel(control_logic_1_alusel), .Result(Arithmetic_Logic_Unit_result), .A(multiplexer_2_out),
    .B(multiplexer_3_out));  // open: out_4
  // mem_main DMEM: pin names not known; wires that end beside it: Arithmetic_Logic_Unit_result, RegFile_read_data_2, CLOCK, control_logic_1_memrw, DMEM_p5
  Multiplexer #(.select(2), .width(32), .enable("false")) multiplexer_4 (
    .in0(DMEM_p5), .in1(Arithmetic_Logic_Unit_result), .in2(adder_1_out), .out(multiplexer_4_out),
    .sel(control_logic_1_wbsel));  // open: in3

  // Other names for the same wires on the sheet: clk = CLOCK

  // Notes on the sheet:
  //   Output
  //   IMEM (do **NOT** move this)
  //   Inputs
  //   It is OK to move the PC, RegFile, ALU, MEM, Branch Comp, Imm Gen, and Control Logic to wherever is most convenient for you when constructing your CPU, and to delete this text
  //   Inputs/Outputs for testing. Do **NOT** move these.
endmodule
