// Logisim project imm_gen.circ as structural Verilog: 1 circuit, main circuit imm_gen
module imm_gen (
  input  [31:0] inst,
  input  [2:0] ImmSel,
  output [31:0] imm
);

  assign imm = {{20{inst[31]}}, inst[31:20]};  // Bit_Extender bit_extender_1

  // Notes on the sheet:
  //   INPUTS to your circuit
  //   simple imm gen for addi only
  //   DON'T CHANGE THE LOCATIONS OF THE INPUTS AND OUTPUTS!
  //   OUTPUT from your circuit
endmodule
